# Fritzing sketch Влажность почвы (saved by Fritzing 0.9.10b)

parts:
  S1 = Round Pushbutton
  U2 = LIPO-1000mAh [package=lipo-1000]
  LM3 = Soil Moisture Sensor
  WeMos_D1_Mini1 = WeMos D1 Mini
  TP1 = TP4056 [chip_label=TP4056 package="DIP (Dual Inline) [THT]"]

nets:
  N1: S1.leg0, TP1.pin3
  VCC: S1.leg1, LM3.VCC, WeMos_D1_Mini1.5V
  N2: U2.+, TP1.pin4
  N3: U2.-, LM3.GND, WeMos_D1_Mini1.G, TP1.pin5, TP1.pin6
  N4: LM3.SIG, WeMos_D1_Mini1.A0

notes:
  Датчик влажности почвы LM393
  Измеряет влажность почвы
  Управляющий контроллер на базе ESP8266
  Подключается по WI-FI к mesh-сети
  Аккумулятор LI-ion 1s1p (литий-полимерный аккумулятор)
  Напряжение 3.7V-4.2V
  Источник питания датчика
  Кнопка питания
  Позволяет отключить питание датчика для защиты аккумулятора и долгосрочного хранения
  Кнопка питания
  Позволяе отключить питание датчика для защиты аккумулятора и долгосрочного хранения
  Аккумулятор LI-ion 1s1p (литий-полимерный аккумулятор)
  Напряжение 2.4V-4.2V
  Источник питания датчика
  Модуль контроля заряда аккумулятора TP4056
  Плата заряда и защиты аккумулятора

custom parts:
  TP4056: A DIP stand-in part for whatever IC you want. With 6 pins on a 300mil dual inline package (DIP) footprint.
