# Fritzing sketch Насос + увл воздуха + датчик уровня воды (saved by Fritzing 0.9.10b)

parts:
  WeMos_D1_Mini1 = WeMos D1 Mini
  J1 = Power Jack [package=power_jack_pth]
  S1 = Round Pushbutton
  U3 = HIH-4030 [package=hih-4030]
  C1 = Ceramic Capacitor [capacitance=100nF voltage=35V package="100 mil [THT, multilayer]"]
  M1 = DC Motor [voltage_(max)=6V voltage_(min)=3V]
  J2 = Piezo Speaker
  Relay_module1 = Relay Module

nets:
  VCC: WeMos_D1_Mini1.5V, S1.leg0, U3.VCC, C1.1, Relay_module1.VCC, Relay_module1.CO
  N1: WeMos_D1_Mini1.A0, U3.OUT
  N2: WeMos_D1_Mini1.D2, J2.pin2
  N3: WeMos_D1_Mini1.D5, Relay_module1.VIN
  GND: WeMos_D1_Mini1.G, J1.GND, J1.GNDBREAK, U3.GND, C1.0, M1.pin_1, J2.pin1, Relay_module1.GND
  N4: J1.PWR, S1.leg1
  N5: M1.pin_2, Relay_module1.NO

notes:
  Ультразвуковой увлажнитель воздуха Ultrasonic Humidifier
  Увлажняет воздух
  Управляющий контроллер на базе ESP8266
  Подключается по WI-FI к mesh-сети
  Блок питания 5V 1.5A
  Питает всю цепь от розетки.
  Кнопка питания
  Позволяет отключить питание датчика для защиты аккумулятора и долгосрочного хранения
  Релейный модуль
  Усиливает напряжение
  Погружной насос noname
  Качает воду из баллона
  Блокировочный конденсатор.
  Защищает от помех, обратного тока и скачков напряжения
  Датчик уровня воды TTP223
  Измеряет уровень воды в баллоне

custom parts:
  Relay Module: Design made by me. Relay made by Dynamo Electronics (Colombia). It handles high power required by some electronic components such as motors and light bulbs.
