# Fritzing sketch Серводвигатель + датчик тока (saved by Fritzing 0.9.10b)

parts:
  S1 = Round Pushbutton
  A71 = ACS712 Low Current Sensor Board v12
  WeMos_D1_Mini1 = WeMos D1 Mini
  J1 = Basic Servo
  J2 = Power Jack [package=power_jack_pth]
  C1 = Ceramic Capacitor [capacitance="100 nF" voltage=35V package="1206 [SMD, multilayer]"]

nets:
  N1: S1.leg0, A71.IP+
  N2: S1.leg1, J2.PWR
  N3: A71.IP-, J1.vcc
  5V: A71.5V, WeMos_D1_Mini1.5V, C1.1
  N4: A71.VO, WeMos_D1_Mini1.A0
  GND: A71.GND, WeMos_D1_Mini1.G, J1.gnd, J2.GND, J2.GNDBREAK, C1.0
  N5: WeMos_D1_Mini1.D2, J1.pulse

notes:
  Серводвигатель DS3230-270.
  Осуществляет поднятие форточки на различные углы ( 30° , 45° , 90° , 110° ).
  Управляющий контроллер на базе ESP8266
  Подключается по WI-FI к mesh-сети
  Кнопка питания
  Позволяет отключить питание датчика для защиты аккумулятора и долгосрочного хранения
  Датчик тока ACS712.
  Замеряет величину тока, проходящего через серводвигатель.
  Блок питания 5V 1.5A
  Питает всю цепь от разетки.
  Датчик тока ACS712.
  Замеряет величину тока, подаваемого на серводвигатель.
  Кнопка питания
  Позволяе отключить питание датчика для защиты аккумулятора и долгосрочного хранения
  Блокировочный конденсатор.
  Защищает от помех, обратного тока и скачков напряжения
  Блокировочный конденсатор.
  Не позволяет току идти в обратном направлении от серводвигателя.
